# Fritzing sketch electronic_thermometer (saved by Fritzing 0.9.2b)
breadboards: 1

parts:
  T1 = LM35 Temperature Sensor [package="TO92 [THT]"]
  Εξάρτημα1 = Arduino Uno (Rev3)
  IC1 = IC, DIP package, 12 pins [chip_label=3641BS]

nets:
  N1: T1.+Vs, Εξάρτημα1.5V
  N2: T1.Vout, Εξάρτημα1.A0
  GND: T1.GND, Εξάρτημα1.GND
  N3: Εξάρτημα1.D8, IC1.pin12
  N4: Εξάρτημα1.D9_PWM, IC1.pin5
  N5: Εξάρτημα1.D10_PWM/SS, IC1.pin6
  N6: Εξάρτημα1.D11_PWM/MOSI, IC1.pin3
  N7: Εξάρτημα1.D12/MISO, IC1.pin9
  N8: Εξάρτημα1.D13/SCK, IC1.pin8
  N9: Εξάρτημα1.D2, IC1.pin10
  N10: Εξάρτημα1.D3_PWM, IC1.pin1
  N11: Εξάρτημα1.D4, IC1.pin2
  N12: Εξάρτημα1.D5_PWM, IC1.pin4
  N13: Εξάρτημα1.D6_PWM, IC1.pin11
  N14: Εξάρτημα1.D7, IC1.pin7
