# Fritzing sketch shift_register_potentiometer (saved by Fritzing 0.9.2b)
breadboards: 2

parts:
  LED1 = LED - 3mm [color="Red (633nm)" package="3 mm [THT]"]
  LED2 = LED - 3mm [color="Red (633nm)" package="3 mm [THT]"]
  LED3 = LED - 3mm [color="Red (633nm)" package="3 mm [THT]"]
  LED4 = LED - 3mm [color="Red (633nm)" package="3 mm [THT]"]
  LED5 = LED - 3mm [color="Red (633nm)" package="3 mm [THT]"]
  LED6 = LED - 3mm [color="Red (633nm)" package="3 mm [THT]"]
  LED7 = LED - 3mm [color="Red (633nm)" package="3 mm [THT]"]
  LED8 = LED - 3mm [color="Red (633nm)" package="3 mm [THT]"]
  R1 = Resistor [tolerance=±5% resistance=220 package=THT]
  R2 = Resistor [tolerance=±5% resistance=220 package=THT]
  R3 = Resistor [tolerance=±5% resistance=220 package=THT]
  R4 = Resistor [tolerance=±5% resistance=220 package=THT]
  R5 = Resistor [tolerance=±5% resistance=220 package=THT]
  R6 = Resistor [tolerance=±5% resistance=220 package=THT]
  R7 = Resistor [tolerance=±5% resistance=220 package=THT]
  R8 = Resistor [tolerance=±5% resistance=220 package=THT]
  R9 = Rotary Potentiometer (Large) [maximum_resistance=10kΩ package=THT]
  IC1 = SHIFT REGISTER [package=dil16]
  Εξάρτημα1 = Arduino Uno (Rev3)

nets:
  GND: LED1.cathode, LED2.cathode, LED3.cathode, LED4.cathode, LED5.cathode, LED6.cathode, LED7.cathode, LED8.cathode, R9.leg2, IC1.GND, Εξάρτημα1.GND
  N1: LED1.anode, R1.Pin_0
  N2: LED2.anode, R2.Pin_0
  N3: LED3.anode, R7.Pin_0
  N4: LED4.anode, R3.Pin_0
  N5: LED5.anode, R4.Pin_0
  N6: LED6.anode, R5.Pin_0
  N7: LED7.anode, R6.Pin_0
  N8: LED8.anode, R8.Pin_0
  N9: R9.leg1, IC1.SCL, Εξάρτημα1.5V
  N10: R9.wiper, Εξάρτημα1.A2
  N11: IC1.SCK, Εξάρτημα1.D12/MISO
  N12: IC1.RCK, Εξάρτημα1.D8
  N13: IC1.G, Εξάρτημα1.D3_PWM
  N14: IC1.SER, Εξάρτημα1.D11_PWM/MOSI
